// Logisim project assign1.circ as structural Verilog: 1 circuit, main circuit main
module main (
  input  in_1,
  input  in_2,
  input  Start_Botton,
  input  in_4,
  input  in_5,
  input  Start_Botton_2,
  input  in_7,
  input  in_8,
  input  in_9,
  input  in_10,
  input  in_11,
  input  in_12,
  input  in_13,
  input  in_14,
  input  in_15,
  input  in_16
);

  wire and_1_out, and_2_out, and_3_out, and_4_out, and_5_out, and_6_out, and_7_out, and_8_out, and_9_out,
       and_10_out, and_11_out, and_12_out, and_13_out, and_14_out, and_15_out, and_16_out, and_17_out,
       and_18_out, and_19_out, and_20_out, and_21_out, and_22_out, and_23_out, and_24_out, and_25_out,
       and_26_out, and_27_out, and_28_out, and_29_out, and_30_out, and_31_out, and_32_out, and_33_out,
       and_34_out, and_35_out, and_36_out, and_37_out, and_38_out, and_39_out, and_40_out, and_41_out,
       button_1_out, button_2_out, button_3_out, button_4_out, clock_1_out, clock_2_out, clock_3_out,
       clock_4_out, d_ff_1_q, d_ff_2_q, d_ff_3_q, d_ff_4_q, d_ff_5_q, d_ff_6_q, j_k_ff_20_qn, j_k_ff_21_qn,
       j_k_ff_23_qn, j_k_ff_24_qn, j_k_ff_31_qn, not_1_out, not_2_out, not_3_out, not_4_out, or_1_out,
       or_2_out, or_3_out, or_4_out, or_5_out, t_ff_1_q, t_ff_2_q, xor_1_out, xor_2_out, xor_3_out, xor_4_out;
  wire [0:0] j_k_ff_2_q, j_k_ff_3_q;
  wire [2:0] j_k_ff_1_q, j_k_ff_5_q, j_k_ff_25_q;
  wire [3:0] j_k_ff_7_q, j_k_ff_10_q, j_k_ff_11_q, j_k_ff_15_q, j_k_ff_28_q;

  Clock clock_1 (.out(clock_1_out));
  Clock clock_2 (.out(clock_2_out));
  Button button_1 (.out(button_1_out));
  Clock clock_3 (.out(clock_3_out));
  Button button_2 (.out(button_2_out));
  Button button_3 (.out(button_3_out));
  not not_1 (not_1_out, in_7);
  and and_1 (and_1_out, and_6_out, j_k_ff_2_q[0]);
  xor xor_1 (xor_1_out, button_1_out, clock_3_out);
  and and_2 (and_2_out, and_8_out, j_k_ff_3_q[0]);
  LED led_1 (.in(j_k_ff_1_q[0]));
  J_K_Flip_Flop j_k_ff_1 (
    .J(d_ff_3_q), .K(d_ff_3_q), .clk(d_ff_3_q), .Q(j_k_ff_1_q[0]), .reset(and_5_out));  // open: Qn, preset
  and and_3 (and_3_out, clock_2_out, not_1_out);
  LED led_2 (.in(j_k_ff_2_q[0]));
  J_K_Flip_Flop j_k_ff_2 (
    .J(d_ff_1_q), .K(d_ff_1_q), .clk(d_ff_1_q), .Q(j_k_ff_2_q[0]), .reset(and_1_out));  // open: Qn, preset
  J_K_Flip_Flop j_k_ff_3 (
    .J(d_ff_2_q), .K(d_ff_2_q), .clk(d_ff_2_q), .Q(j_k_ff_3_q[0]), .reset(and_2_out));  // open: Qn, preset
  xor xor_2 (xor_2_out, button_2_out, d_ff_5_q);
  J_K_Flip_Flop j_k_ff_4 (
    .J(j_k_ff_1_q[0]), .K(j_k_ff_1_q[0]), .clk(d_ff_3_q), .Q(j_k_ff_1_q[1]), .reset(and_5_out));  // open: Qn, preset
  xor xor_3 (xor_3_out, button_3_out, and_3_out);
  LED led_3 (.in(j_k_ff_3_q[0]));
  LED led_4 (.in(j_k_ff_1_q[1]));
  and and_4 (and_4_out, j_k_ff_1_q[1], j_k_ff_1_q[0]);
  J_K_Flip_Flop j_k_ff_5 (
    .J(d_ff_4_q), .K(d_ff_4_q), .clk(d_ff_4_q), .Q(j_k_ff_5_q[0]), .reset(and_13_out));  // open: Qn, preset
  D_Flip_Flop d_ff_1 (.D(and_7_out), .clk(xor_1_out), .Q(d_ff_1_q));  // open: Qn, preset, reset
  D_Flip_Flop d_ff_2 (.D(and_9_out), .clk(xor_2_out), .Q(d_ff_2_q));  // open: Qn, preset, reset
  LED led_5 (.in(j_k_ff_1_q[2]));
  J_K_Flip_Flop j_k_ff_6 (
    .J(and_4_out), .K(and_4_out), .clk(d_ff_3_q), .Q(j_k_ff_1_q[2]), .reset(and_5_out));  // open: Qn, preset
  LED led_6 (.in(j_k_ff_5_q[0]));
  and and_5 (and_5_out, j_k_ff_1_q[1], j_k_ff_1_q[2]);
  J_K_Flip_Flop j_k_ff_7 (
    .J(Start_Botton), .K(Start_Botton), .clk(clock_1_out), .Q(j_k_ff_7_q[0]));  // open: Qn, preset, reset
  D_Flip_Flop d_ff_3 (.D(and_11_out), .clk(clock_1_out), .Q(d_ff_3_q));  // open: Qn, preset, reset
  LED led_7 (.in(j_k_ff_5_q[1]));
  J_K_Flip_Flop j_k_ff_8 (
    .J(j_k_ff_5_q[0]), .K(j_k_ff_5_q[0]), .clk(d_ff_4_q), .Q(j_k_ff_5_q[1]), .reset(and_13_out));  // open: Qn, preset
  Hex_Digit_Display hex_digit_display_1 (.value({{3{in_9}}, j_k_ff_2_q[0]}));  // open: dp
  Hex_Digit_Display hex_digit_display_2 (.value(j_k_ff_10_q));  // open: dp
  and and_6 (and_6_out, j_k_ff_10_q[1], j_k_ff_10_q[0]);
  and and_7 (and_7_out, j_k_ff_10_q[0], j_k_ff_10_q[3]);
  and and_8 (and_8_out, j_k_ff_11_q[1], j_k_ff_11_q[0]);
  and and_9 (and_9_out, j_k_ff_11_q[0], j_k_ff_11_q[3]);
  Hex_Digit_Display hex_digit_display_3 (.value({in_1, j_k_ff_1_q}));  // open: dp
  LED led_8 (.in(j_k_ff_7_q[0]));
  and and_10 (and_10_out, j_k_ff_7_q[0], j_k_ff_20_qn);
  and and_11 (and_11_out, j_k_ff_7_q[0], j_k_ff_7_q[3]);
  and and_12 (and_12_out, j_k_ff_5_q[1], j_k_ff_5_q[0]);
  J_K_Flip_Flop j_k_ff_9 (
    .J(and_12_out), .K(and_12_out), .clk(d_ff_4_q), .Q(j_k_ff_5_q[2]), .reset(and_13_out));  // open: Qn, preset
  LED led_9 (.in(j_k_ff_10_q[0]));
  J_K_Flip_Flop j_k_ff_10 (.J(in_8), .K(in_8), .clk(xor_1_out), .Q(j_k_ff_10_q[0]));  // open: Qn, preset, reset
  J_K_Flip_Flop j_k_ff_11 (
    .J(xor_2_out), .K(xor_2_out), .clk(xor_2_out), .Q(j_k_ff_11_q[0]));  // open: Qn, preset, reset
  Hex_Digit_Display hex_digit_display_4 (.value(j_k_ff_7_q));  // open: dp
  LED led_10 (.in(j_k_ff_7_q[1]));
  J_K_Flip_Flop j_k_ff_12 (
    .J(and_10_out), .K(and_10_out), .clk(clock_1_out), .Q(j_k_ff_7_q[1]));  // open: Qn, preset, reset
  LED led_11 (.in(j_k_ff_5_q[2]));
  and and_13 (and_13_out, j_k_ff_5_q[1], j_k_ff_5_q[2]);
  D_Flip_Flop d_ff_4 (.D(and_19_out), .clk(xor_3_out), .Q(d_ff_4_q));  // open: Qn, preset, reset
  not not_2 (not_2_out, t_ff_1_q);
  LED led_12 (.in(not_2_out));
  LED led_13 (.in(t_ff_1_q));
  T_Flip_Flop t_ff_1 (.T(and_14_out), .clk(xor_1_out), .Q(t_ff_1_q));  // open: Qn, reset, preset
  and and_14 (and_14_out, j_k_ff_2_q[0], j_k_ff_10_q[0]);
  J_K_Flip_Flop j_k_ff_13 (
    .J(and_15_out), .K(and_15_out), .clk(xor_1_out), .Q(j_k_ff_10_q[1]), .reset(and_1_out));  // open: Qn, preset
  and and_15 (and_15_out, j_k_ff_10_q[0], j_k_ff_21_qn);
  T_Flip_Flop t_ff_2 (.T(and_16_out), .clk(xor_2_out), .Q(t_ff_2_q));  // open: Qn, reset, preset
  and and_16 (and_16_out, j_k_ff_3_q[0], j_k_ff_11_q[0]);
  LED led_14 (.in(j_k_ff_11_q[0]));
  and and_17 (and_17_out, j_k_ff_11_q[0], j_k_ff_23_qn);
  and and_18 (and_18_out, j_k_ff_7_q[0], j_k_ff_7_q[1]);
  J_K_Flip_Flop j_k_ff_14 (
    .J(and_18_out), .K(and_18_out), .clk(clock_1_out), .Q(j_k_ff_7_q[2]));  // open: Qn, preset, reset
  LED led_15 (.in(j_k_ff_15_q[0]));
  J_K_Flip_Flop j_k_ff_15 (
    .J(Start_Botton_2), .K(Start_Botton_2), .clk(xor_3_out), .Q(j_k_ff_15_q[0]));  // open: Qn, preset, reset
  and and_19 (and_19_out, j_k_ff_15_q[0], j_k_ff_15_q[3]);
  LED led_16 (.in(j_k_ff_10_q[1]));
  and and_20 (and_20_out, j_k_ff_10_q[0], j_k_ff_10_q[1]);
  LED led_17 (.in(j_k_ff_11_q[1]));
  J_K_Flip_Flop j_k_ff_16 (
    .J(and_17_out), .K(and_17_out), .clk(xor_2_out), .Q(j_k_ff_11_q[1]), .reset(and_2_out));  // open: Qn, preset
  LED led_18 (.in(j_k_ff_7_q[2]));
  and and_21 (and_21_out, j_k_ff_7_q[3], j_k_ff_7_q[0]);
  and and_22 (and_22_out, and_18_out, j_k_ff_7_q[2]);
  Hex_Digit_Display hex_digit_display_5 (.value({in_4, j_k_ff_5_q}));  // open: dp
  Hex_Digit_Display hex_digit_display_6 (.value(j_k_ff_15_q));  // open: dp
  J_K_Flip_Flop j_k_ff_17 (
    .J(and_23_out), .K(and_23_out), .clk(xor_3_out), .Q(j_k_ff_15_q[1]));  // open: Qn, preset, reset
  and and_23 (and_23_out, j_k_ff_15_q[0], j_k_ff_24_qn);
  LED led_19 (.in(j_k_ff_10_q[2]));
  J_K_Flip_Flop j_k_ff_18 (
    .J(and_20_out), .K(and_20_out), .clk(xor_1_out), .Q(j_k_ff_10_q[2]));  // open: Qn, preset, reset
  and and_24 (and_24_out, j_k_ff_11_q[0], j_k_ff_11_q[1]);
  J_K_Flip_Flop j_k_ff_19 (
    .J(and_24_out), .K(and_24_out), .clk(xor_2_out), .Q(j_k_ff_11_q[2]));  // open: Qn, preset, reset
  or or_1 (or_1_out, and_21_out, and_22_out);
  J_K_Flip_Flop j_k_ff_20 (
    .J(or_1_out), .K(or_1_out), .clk(clock_1_out), .Q(j_k_ff_7_q[3]), .Qn(j_k_ff_20_qn));  // open: preset, reset
  LED led_20 (.in(j_k_ff_15_q[1]));
  and and_25 (and_25_out, j_k_ff_15_q[0], j_k_ff_15_q[1]);
  and and_26 (and_26_out, j_k_ff_10_q[3], j_k_ff_10_q[0]);
  or or_2 (or_2_out, and_26_out, and_27_out);
  and and_27 (and_27_out, and_20_out, j_k_ff_10_q[2]);
  J_K_Flip_Flop j_k_ff_21 (
    .J(or_2_out), .K(or_2_out), .clk(xor_1_out), .Q(j_k_ff_10_q[3]), .Qn(j_k_ff_21_qn));  // open: preset, reset
  LED led_21 (.in(j_k_ff_11_q[2]));
  and and_28 (and_28_out, j_k_ff_11_q[3], j_k_ff_11_q[0]);
  and and_29 (and_29_out, and_24_out, j_k_ff_11_q[2]);
  LED led_22 (.in(j_k_ff_7_q[3]));
  LED led_23 (.in(j_k_ff_15_q[2]));
  J_K_Flip_Flop j_k_ff_22 (
    .J(and_25_out), .K(and_25_out), .clk(xor_3_out), .Q(j_k_ff_15_q[2]));  // open: Qn, preset, reset
  LED led_24 (.in(j_k_ff_10_q[3]));
  LED led_25 (.in(j_k_ff_11_q[3]));
  or or_3 (or_3_out, and_28_out, and_29_out);
  J_K_Flip_Flop j_k_ff_23 (
    .J(or_3_out), .K(or_3_out), .clk(xor_2_out), .Q(j_k_ff_11_q[3]), .Qn(j_k_ff_23_qn));  // open: preset, reset
  and and_30 (and_30_out, j_k_ff_15_q[3], j_k_ff_15_q[0]);
  or or_4 (or_4_out, and_30_out, and_31_out);
  and and_31 (and_31_out, and_25_out, j_k_ff_15_q[2]);
  J_K_Flip_Flop j_k_ff_24 (
    .J(or_4_out), .K(or_4_out), .clk(xor_3_out), .Q(j_k_ff_15_q[3]), .Qn(j_k_ff_24_qn));  // open: preset, reset
  LED led_26 (.in(j_k_ff_15_q[3]));
  Clock clock_4 (.out(clock_4_out));
  Hex_Digit_Display hex_digit_display_7 (.value({{3{in_13}}, j_k_ff_3_q[0]}));  // open: dp
  not not_3 (not_3_out, in_16);
  D_Flip_Flop d_ff_5 (.D(and_33_out), .clk(clock_4_out), .Q(d_ff_5_q));  // open: Qn, preset, reset
  Hex_Digit_Display hex_digit_display_8 (.value(j_k_ff_11_q));  // open: dp
  Button button_4 (.out(button_4_out));
  and and_32 (and_32_out, clock_4_out, not_3_out);
  Hex_Digit_Display hex_digit_display_9 (.value({in_12, j_k_ff_25_q}));  // open: dp
  Hex_Digit_Display hex_digit_display_10 (.value(j_k_ff_28_q));  // open: dp
  xor xor_4 (xor_4_out, button_4_out, and_32_out);
  and and_33 (and_33_out, and_34_out, and_38_out);
  LED led_27 (.in(not_4_out));
  LED led_28 (.in(t_ff_2_q));
  J_K_Flip_Flop j_k_ff_25 (
    .J(d_ff_6_q), .K(d_ff_6_q), .clk(d_ff_6_q), .Q(j_k_ff_25_q[0]), .reset(and_36_out));  // open: Qn, preset
  not not_4 (not_4_out, t_ff_2_q);
  LED led_29 (.in(j_k_ff_25_q[0]));
  and and_34 (and_34_out, j_k_ff_25_q[0], j_k_ff_25_q[2]);
  LED led_30 (.in(j_k_ff_25_q[1]));
  J_K_Flip_Flop j_k_ff_26 (
    .J(j_k_ff_25_q[0]), .K(j_k_ff_25_q[0]), .clk(d_ff_6_q), .Q(j_k_ff_25_q[1]), .reset(and_36_out));  // open: Qn, preset
  and and_35 (and_35_out, j_k_ff_25_q[1], j_k_ff_25_q[0]);
  J_K_Flip_Flop j_k_ff_27 (
    .J(and_35_out), .K(and_35_out), .clk(d_ff_6_q), .Q(j_k_ff_25_q[2]), .reset(and_36_out));  // open: Qn, preset
  LED led_31 (.in(j_k_ff_25_q[2]));
  and and_36 (and_36_out, j_k_ff_25_q[1], j_k_ff_25_q[2]);
  D_Flip_Flop d_ff_6 (.D(and_38_out), .clk(xor_4_out), .Q(d_ff_6_q));  // open: Qn, preset, reset
  J_K_Flip_Flop j_k_ff_28 (.J(in_11), .K(in_11), .clk(xor_4_out), .Q(j_k_ff_28_q[0]));  // open: Qn, preset, reset
  LED led_32 (.in(j_k_ff_28_q[0]));
  and and_37 (and_37_out, j_k_ff_28_q[0], j_k_ff_31_qn);
  and and_38 (and_38_out, j_k_ff_28_q[0], j_k_ff_28_q[3]);
  LED led_33 (.in(j_k_ff_28_q[1]));
  J_K_Flip_Flop j_k_ff_29 (
    .J(and_37_out), .K(and_37_out), .clk(xor_4_out), .Q(j_k_ff_28_q[1]));  // open: Qn, preset, reset
  and and_39 (and_39_out, j_k_ff_28_q[0], j_k_ff_28_q[1]);
  J_K_Flip_Flop j_k_ff_30 (
    .J(and_39_out), .K(and_39_out), .clk(xor_4_out), .Q(j_k_ff_28_q[2]));  // open: Qn, preset, reset
  LED led_34 (.in(j_k_ff_28_q[2]));
  and and_40 (and_40_out, j_k_ff_28_q[3], j_k_ff_28_q[0]);
  and and_41 (and_41_out, and_39_out, j_k_ff_28_q[2]);
  LED led_35 (.in(j_k_ff_28_q[3]));
  or or_5 (or_5_out, and_40_out, and_41_out);
  J_K_Flip_Flop j_k_ff_31 (
    .J(or_5_out), .K(or_5_out), .clk(xor_4_out), .Q(j_k_ff_28_q[3]), .Qn(j_k_ff_31_qn));  // open: preset, reset

  // Notes on the sheet:
  //   bit from 1 and 3
  //   to pass to reset 
  //   button
  //   button
  //   Stage 1
  //   Clock
  //   Stage 2
  //   Clock
  //   Stage 3
  //   Start Botton
  //   AND gate combining
  //   h+ Button to increment hour
  //   Clock
  //   Start Botton
  //   AND gate combining
  //   bit from 1 and 3
  //   to pass to reset 
  //   h+ Button to increment hour
  //   m+ Button to increment minute
  //   "Set time" Pin to pause the minute
  //   Stage 4
  //   "Tens" counter
  //   "Tens" counter
  //   JK flip flop output toggling
  //   JK flip flop output toggling
  //   D Flip Flop to avoid Illegal State
  //   Link goes to reset button to output binary 2
  //   Link goes to reset button to output binary 2
  //   "Tens" counter
  //   D Flip Flop to avoid Illegal State
  //   D Flip Flop to avoid Illegal State
  //   Positive bit from "59" display will be sent to the input of the hour counter, acting as a clock pulse
  //   AM
  //   PM
  //   D Flip Flop to avoid Illegal State
  //   "Units" counter
  //   AND Gate passing one bit from 8 and 1 binary output
  //   "Units" counter
  //   AND Gate passing one bit from 8 and 1 binary output
  //   AND Gate passing one bit from 8 and 1 binary output
  //   AM, PM settings done via T flip flop
  //   AM, PM settings done via T flip flop
  //   "Units" counter
  //   AND Gate passing one bit from 8 and 1 binary output
  //   Clock
  //   m+ Button to increment minute
  //   "Set time" Pin to pause the minute
  //   D Flip Flop to avoid Illegal State
  //   :
  //   AM
  //   PM
  //   AND Gate passing one bit from 5 and 9 binary output from each individual counter
  //   D Flip Flop to avoid Illegal State
  //   AND Gate passing one bit from 8 and 1 binary output
endmodule
