// Logisim project AND_Gate.circ as structural Verilog: 1 circuit, main circuit main
module main (
  input  in_1,
  input  in_2,
  input  in_3,
  input  in_4,
  input  in_5,
  input  in_6,
  input  in_7,
  input  in_8
);

  wire and_1_out, and_2_out, and_3_out, and_4_out;

  and and_1 (and_1_out, in_1, in_3);
  LED led_1 (.in(and_1_out));
  and and_2 (and_2_out, in_5, in_7);
  LED led_2 (.in(and_2_out));
  and and_3 (and_3_out, in_2, in_4);
  and and_4 (and_4_out, in_6, in_8);
  LED led_3 (.in(and_3_out));
  LED led_4 (.in(and_4_out));
endmodule
