// Logisim project Full_adder.circ as structural Verilog: 1 circuit, main circuit main
module main (
  input  C_in,
  input  C_in_2,
  input  Input_1,
  input  Input_1_2,
  input  Input_2,
  input  Input_2_2,
  input  C_in_3,
  input  C_in_4,
  input  Input_1_3,
  input  Input_1_4,
  input  Input_2_3,
  input  Input_2_4,
  input  C_in_5,
  input  C_in_6,
  input  Input_1_5,
  input  Input_1_6,
  input  Input_2_5,
  input  Input_2_6,
  input  C_in_7,
  input  C_in_8,
  input  Input_1_7,
  input  Input_1_8,
  input  Input_2_7,
  input  Input_2_8
);

  wire and_1_out, and_2_out, and_3_out, and_4_out, and_5_out, and_6_out, and_7_out, and_8_out, and_9_out,
       and_10_out, and_11_out, and_12_out, and_13_out, and_14_out, and_15_out, and_16_out, or_1_out,
       or_2_out, or_3_out, or_4_out, or_5_out, or_6_out, or_7_out, or_8_out, xor_1_out, xor_2_out, xor_3_out,
       xor_4_out, xor_5_out, xor_6_out, xor_7_out, xor_8_out, xor_9_out, xor_10_out, xor_11_out, xor_12_out,
       xor_13_out, xor_14_out, xor_15_out, xor_16_out;

  xor xor_1 (xor_1_out, Input_1, Input_2);
  and and_1 (and_1_out, Input_1, Input_2);
  xor xor_2 (xor_2_out, Input_1_3, Input_2_3);
  and and_2 (and_2_out, Input_1_3, Input_2_3);
  xor xor_3 (xor_3_out, Input_1_5, Input_2_5);
  and and_3 (and_3_out, Input_1_5, Input_2_5);
  xor xor_4 (xor_4_out, Input_1_7, Input_2_7);
  and and_4 (and_4_out, Input_1_7, Input_2_7);
  xor xor_5 (xor_5_out, C_in, xor_1_out);
  and and_5 (and_5_out, C_in, xor_1_out);
  xor xor_6 (xor_6_out, C_in_3, xor_2_out);
  and and_6 (and_6_out, C_in_3, xor_2_out);
  xor xor_7 (xor_7_out, C_in_5, xor_3_out);
  and and_7 (and_7_out, C_in_5, xor_3_out);
  xor xor_8 (xor_8_out, C_in_7, xor_4_out);
  and and_8 (and_8_out, C_in_7, xor_4_out);
  LED led_1 (.in(xor_5_out));
  or or_1 (or_1_out, and_5_out, and_1_out);
  LED led_2 (.in(or_1_out));
  LED led_3 (.in(xor_6_out));
  or or_2 (or_2_out, and_6_out, and_2_out);
  LED led_4 (.in(or_2_out));
  LED led_5 (.in(xor_7_out));
  or or_3 (or_3_out, and_7_out, and_3_out);
  LED led_6 (.in(or_3_out));
  LED led_7 (.in(xor_8_out));
  or or_4 (or_4_out, and_8_out, and_4_out);
  LED led_8 (.in(or_4_out));
  xor xor_9 (xor_9_out, Input_1_2, Input_2_2);
  and and_9 (and_9_out, Input_1_2, Input_2_2);
  xor xor_10 (xor_10_out, Input_1_4, Input_2_4);
  and and_10 (and_10_out, Input_1_4, Input_2_4);
  xor xor_11 (xor_11_out, Input_1_6, Input_2_6);
  and and_11 (and_11_out, Input_1_6, Input_2_6);
  xor xor_12 (xor_12_out, Input_1_8, Input_2_8);
  and and_12 (and_12_out, Input_1_8, Input_2_8);
  xor xor_13 (xor_13_out, C_in_2, xor_9_out);
  and and_13 (and_13_out, C_in_2, xor_9_out);
  xor xor_14 (xor_14_out, C_in_4, xor_10_out);
  and and_14 (and_14_out, C_in_4, xor_10_out);
  xor xor_15 (xor_15_out, C_in_6, xor_11_out);
  and and_15 (and_15_out, C_in_6, xor_11_out);
  xor xor_16 (xor_16_out, C_in_8, xor_12_out);
  and and_16 (and_16_out, C_in_8, xor_12_out);
  LED led_9 (.in(xor_13_out));
  or or_5 (or_5_out, and_13_out, and_9_out);
  LED led_10 (.in(or_5_out));
  LED led_11 (.in(xor_14_out));
  or or_6 (or_6_out, and_14_out, and_10_out);
  LED led_12 (.in(or_6_out));
  LED led_13 (.in(xor_15_out));
  or or_7 (or_7_out, and_15_out, and_11_out);
  LED led_14 (.in(or_7_out));
  LED led_15 (.in(xor_16_out));
  or or_8 (or_8_out, and_16_out, and_12_out);
  LED led_16 (.in(or_8_out));

  // Notes on the sheet:
  //   Sum Out
  //   C out
  //   Sum Out
  //   C out
  //   Sum Out
  //   C out
  //   Sum Out
  //   C out
  //   Sum Out
  //   C out
  //   Sum Out
  //   C out
  //   Sum Out
  //   C out
  //   Sum Out
  //   C out
endmodule
