// Logisim project HalfAdder.circ as structural Verilog: 1 circuit, main circuit main
module main (
  input  Pin_1,
  input  Pin_1_2,
  input  Pin2,
  input  Pin2_2,
  input  Pin_1_3,
  input  Pin_1_4,
  input  Pin2_3,
  input  Pin2_4
);

  wire and_1_out, and_2_out, and_3_out, and_4_out, xor_1_out, xor_2_out, xor_3_out, xor_4_out;

  xor xor_1 (xor_1_out, Pin_1, Pin2);
  LED led_1 (.in(xor_1_out));
  and and_1 (and_1_out, Pin2, Pin_1);
  LED led_2 (.in(and_1_out));
  xor xor_2 (xor_2_out, Pin_1_3, Pin2_3);
  LED led_3 (.in(xor_2_out));
  and and_2 (and_2_out, Pin2_3, Pin_1_3);
  LED led_4 (.in(and_2_out));
  xor xor_3 (xor_3_out, Pin_1_2, Pin2_2);
  and and_3 (and_3_out, Pin2_2, Pin_1_2);
  xor xor_4 (xor_4_out, Pin_1_4, Pin2_4);
  and and_4 (and_4_out, Pin2_4, Pin_1_4);
  LED led_5 (.in(xor_3_out));
  LED led_6 (.in(and_3_out));
  LED led_7 (.in(xor_4_out));
  LED led_8 (.in(and_4_out));

  // Notes on the sheet:
  //   Half Adder
  //   Sum
  //   C out
  //   Sum
  //   C out
  //   Sum
  //   C out
  //   Sum
  //   C out
endmodule
