// Logisim project NAND_Gate.circ as structural Verilog: 1 circuit, main circuit main
module main (
  input  in_1,
  input  in_2,
  input  in_3,
  input  in_4,
  input  in_5,
  input  in_6,
  input  in_7,
  input  in_8
);

  wire nand_1_out, nand_2_out, nand_3_out, nand_5_out;

  nand nand_1 (nand_1_out, in_1, in_3);
  LED led_1 (.in(nand_1_out));
  nand nand_2 (nand_2_out, in_5, in_7);
  LED led_2 (.in(nand_2_out));
  nand nand_3 (nand_3_out, in_2, in_4);
  nand nand_4 (nand_3_out, in_2, in_4);
  LED led_3 (.in(nand_3_out));
  nand nand_5 (nand_5_out, in_6, in_8);
  LED led_4 (.in(nand_5_out));
endmodule
