// Logisim project NOT_Gate.circ as structural Verilog: 1 circuit, main circuit main
module main (
  input  in_1,
  input  in_2
);

  wire not_1_out, not_2_out;

  not not_1 (not_1_out, in_1);
  not not_2 (not_2_out, in_2);
  LED led_1 (.in(not_1_out));
  LED led_2 (.in(not_2_out));
endmodule
