// Logisim project 4_bits.circ as structural Verilog: 1 circuit, main circuit main
module main (
  input  X0,
  input  Y0,
  input  X1,
  input  Y1,
  input  X2,
  input  Y2,
  input  X3,
  input  Y3
);

  wire and_1_out, and_2_out, and_3_out, and_4_out, and_5_out, and_6_out, and_7_out, or_1_out, or_2_out,
       or_3_out, xor_1_out, xor_2_out, xor_3_out, xor_4_out, xor_5_out, xor_6_out, xor_7_out;

  xor xor_1 (xor_1_out, X0, Y0);
  and and_1 (and_1_out, Y0, X0);
  xor xor_2 (xor_2_out, X1, Y1);
  and and_2 (and_2_out, X1, Y1);
  xor xor_3 (xor_3_out, X2, Y2);
  and and_3 (and_3_out, X2, Y2);
  xor xor_4 (xor_4_out, X3, Y3);
  and and_4 (and_4_out, X3, Y3);
  LED led_1 (.in(xor_1_out));
  xor xor_5 (xor_5_out, and_1_out, xor_2_out);
  and and_5 (and_5_out, and_1_out, xor_2_out);
  xor xor_6 (xor_6_out, or_1_out, xor_3_out);
  and and_6 (and_6_out, or_1_out, xor_3_out);
  xor xor_7 (xor_7_out, or_2_out, xor_4_out);
  and and_7 (and_7_out, or_2_out, xor_4_out);
  LED led_2 (.in(xor_5_out));
  or or_1 (or_1_out, and_5_out, and_2_out);
  LED led_3 (.in(xor_6_out));
  or or_2 (or_2_out, and_6_out, and_3_out);
  LED led_4 (.in(xor_7_out));
  or or_3 (or_3_out, and_7_out, and_4_out);
  LED led_5 (.in(or_3_out));

  // Notes on the sheet:
  //   Sum Out 0
  //   Sum Out 1
  //   C out
  //   Sum Out 2
  //   C out
  //   Sum Out 3
  //   C out
endmodule
