// Logisim project JK_flipflop2.circ as structural Verilog: 1 circuit, main circuit main
module main (
  input  in_1,
  input  in_2
);

  wire clock_1_out, j_k_ff_1_q, j_k_ff_1_qn;

  Clock clock_1 (.out(clock_1_out));
  J_K_Flip_Flop j_k_ff_1 (
    .J(in_1), .K(clock_1_out), .clk(in_2), .Q(j_k_ff_1_q), .Qn(j_k_ff_1_qn));  // open: preset, reset
  LED led_1 (.in(j_k_ff_1_q));
  LED led_2 (.in(j_k_ff_1_qn));
endmodule
