// Logisim project 0_5_clock.circ as structural Verilog: 1 circuit, main circuit main
module main (
  input  in_1
);

  wire and_1_out, and_2_out, clock_1_out, j_k_ff_1_q, j_k_ff_2_q, j_k_ff_3_q;

  Clock clock_1 (.out(clock_1_out));
  J_K_Flip_Flop #(.trigger("falling")) j_k_ff_1 (
    .J(in_1), .K(in_1), .clk(clock_1_out), .Q(j_k_ff_1_q), .reset(and_2_out));  // open: Qn, preset
  LED led_1 (.in(j_k_ff_1_q));
  J_K_Flip_Flop #(.trigger("falling")) j_k_ff_2 (
    .J(j_k_ff_1_q), .K(j_k_ff_1_q), .clk(clock_1_out), .Q(j_k_ff_2_q), .reset(and_2_out));  // open: Qn, preset
  LED led_2 (.in(j_k_ff_2_q));
  and and_1 (and_1_out, j_k_ff_1_q, j_k_ff_2_q);
  J_K_Flip_Flop #(.trigger("falling")) j_k_ff_3 (
    .J(and_1_out), .K(and_1_out), .clk(clock_1_out), .Q(j_k_ff_3_q), .reset(and_2_out));  // open: Qn, preset
  LED led_3 (.in(j_k_ff_3_q));
  and and_2 (and_2_out, j_k_ff_3_q, j_k_ff_2_q);

  // Notes on the sheet:
  //   1
  //   2
  //   4
endmodule
