// Logisim project Clock_without_illegal_state_with_hexadecimaldispaly.circ as structural Verilog: 1 circuit, main circuit main
module main (
  input  in_1,
  input  in_2
);

  wire and_1_out, and_2_out, and_3_out, and_4_out, and_5_out, and_6_out, and_7_out, and_8_out, clock_1_out,
       d_ff_1_q, d_ff_2_q, d_ff_3_q, d_ff_4_q, d_ff_5_q, d_ff_6_q, d_ff_7_q, d_ff_8_q, j_k_ff_1_q,
       j_k_ff_2_q, j_k_ff_3_q, j_k_ff_4_q, j_k_ff_5_q, j_k_ff_6_q, j_k_ff_7_q, j_k_ff_8_q;
  wire [3:0] and_9_out;

  Clock clock_1 (.out(clock_1_out));
  J_K_Flip_Flop #(.trigger("falling")) j_k_ff_1 (
    .J(in_1), .K(in_1), .clk(clock_1_out), .Q(j_k_ff_1_q), .reset(and_7_out));  // open: Qn, preset
  J_K_Flip_Flop #(.trigger("falling")) j_k_ff_2 (
    .J(in_1), .K(in_1), .clk(clock_1_out), .Q(j_k_ff_2_q), .reset(and_8_out));  // open: Qn, preset
  LED led_1 (.in(j_k_ff_1_q));
  LED led_2 (.in(j_k_ff_2_q));
  J_K_Flip_Flop #(.trigger("falling")) j_k_ff_3 (
    .J(j_k_ff_1_q), .K(j_k_ff_1_q), .clk(clock_1_out), .Q(j_k_ff_3_q), .reset(and_7_out));  // open: Qn, preset
  D_Flip_Flop d_ff_1 (.D(j_k_ff_1_q), .clk(clock_1_out), .Q(d_ff_1_q));  // open: Qn, preset, reset
  J_K_Flip_Flop #(.trigger("falling")) j_k_ff_4 (
    .J(j_k_ff_2_q), .K(j_k_ff_2_q), .clk(clock_1_out), .Q(j_k_ff_4_q), .reset(and_8_out));  // open: Qn, preset
  D_Flip_Flop d_ff_2 (.D(j_k_ff_2_q), .clk(clock_1_out), .Q(d_ff_2_q));  // open: Qn, preset, reset
  LED led_3 (.in(j_k_ff_3_q));
  D_Flip_Flop d_ff_3 (.D(j_k_ff_3_q), .clk(clock_1_out), .Q(d_ff_3_q));  // open: Qn, preset, reset
  LED led_4 (.in(j_k_ff_4_q));
  D_Flip_Flop d_ff_4 (.D(j_k_ff_4_q), .clk(clock_1_out), .Q(d_ff_4_q));  // open: Qn, preset, reset
  and and_1 (and_1_out, j_k_ff_1_q, j_k_ff_3_q);
  J_K_Flip_Flop #(.trigger("falling")) j_k_ff_5 (
    .J(and_1_out), .K(and_1_out), .clk(clock_1_out), .Q(j_k_ff_5_q), .reset(and_7_out));  // open: Qn, preset
  and and_2 (and_2_out, j_k_ff_2_q, j_k_ff_4_q);
  J_K_Flip_Flop #(.trigger("falling")) j_k_ff_6 (
    .J(and_2_out), .K(and_2_out), .clk(clock_1_out), .Q(j_k_ff_6_q), .reset(and_8_out));  // open: Qn, preset
  and and_3 (and_3_out, and_1_out, j_k_ff_5_q);
  LED led_5 (.in(j_k_ff_5_q));
  and and_4 (and_4_out, and_2_out, j_k_ff_6_q);
  LED led_6 (.in(j_k_ff_6_q));
  D_Flip_Flop d_ff_5 (.D(j_k_ff_5_q), .clk(clock_1_out), .Q(d_ff_5_q));  // open: Qn, preset, reset
  D_Flip_Flop d_ff_6 (.D(j_k_ff_6_q), .clk(clock_1_out), .Q(d_ff_6_q));  // open: Qn, preset, reset
  and and_5 (and_5_out, j_k_ff_1_q, and_1_out);
  J_K_Flip_Flop j_k_ff_7 (.J(and_3_out), .K(and_3_out), .Q(j_k_ff_7_q), .reset(and_7_out));  // open: clk, Qn, preset
  D_Flip_Flop d_ff_7 (.D(j_k_ff_7_q), .clk(clock_1_out), .Q(d_ff_7_q));  // open: Qn, preset, reset
  and and_6 (and_6_out, j_k_ff_2_q, and_2_out);
  J_K_Flip_Flop j_k_ff_8 (.J(and_4_out), .K(and_4_out), .Q(j_k_ff_8_q), .reset(and_8_out));  // open: clk, Qn, preset
  D_Flip_Flop d_ff_8 (.D(j_k_ff_8_q), .clk(clock_1_out), .Q(d_ff_8_q));  // open: Qn, preset, reset
  and and_7 (and_7_out, j_k_ff_7_q, and_5_out);
  LED led_7 (.in(j_k_ff_7_q));
  LED led_8 (.in(j_k_ff_8_q));
  and and_8 (and_8_out, j_k_ff_8_q, and_6_out);
  and and_9 (and_9_out[0], d_ff_7_q, d_ff_8_q);
  and and_10 (and_9_out[2], d_ff_3_q, d_ff_4_q);
  and and_11 (and_9_out[3], d_ff_5_q, d_ff_6_q);
  and and_12 (and_9_out[1], d_ff_1_q, d_ff_2_q);
  Hex_Digit_Display hex_digit_display_1 (.value(and_9_out));  // open: dp

  // Notes on the sheet:
  //   1
  //   1
  //   2
  //   2
  //   4
  //   4
endmodule
