// Logisim project register1.circ as structural Verilog: 1 circuit, main circuit main
module main (
  input  data,
  input  in_2,
  input  in_3,
  input  in_4,
  input  Pull_to_reset
);

  wire clock_1_out, d_ff_1_q, d_ff_2_q, d_ff_3_q, d_ff_4_q;

  Clock clock_1 (.out(clock_1_out));
  D_Flip_Flop d_ff_1 (.D(data), .clk(clock_1_out), .Q(d_ff_1_q), .reset(Pull_to_reset));  // open: Qn, preset
  LED led_1 (.in(d_ff_1_q));
  D_Flip_Flop d_ff_2 (.D(in_2), .clk(clock_1_out), .Q(d_ff_2_q), .reset(Pull_to_reset));  // open: Qn, preset
  D_Flip_Flop d_ff_3 (.D(in_3), .clk(clock_1_out), .Q(d_ff_3_q), .reset(Pull_to_reset));  // open: Qn, preset
  LED led_2 (.in(d_ff_2_q));
  LED led_3 (.in(d_ff_3_q));
  D_Flip_Flop d_ff_4 (.D(in_4), .clk(clock_1_out), .Q(d_ff_4_q), .reset(Pull_to_reset));  // open: Qn, preset
  LED led_4 (.in(d_ff_4_q));

  // Notes on the sheet:
  //   Clock
  //   8
  //   4 Bits Register
  //   4
  //   2
  //   1
endmodule
