// Logisim project one_directional_stack_and_encoder.circ as structural Verilog: 1 circuit, main circuit main
module main (
  input  Data_In,
  input  in_2,
  input  Input_In,
  input  in_4,
  input  in_5,
  input  in_6,
  input  in_7
);

  wire and_1_out, and_2_out, clock_1_out, clock_2_out, d_ff_1_q, d_ff_2_q, d_ff_3_q, d_ff_4_q, d_ff_5_q,
       d_ff_6_q, d_ff_7_q, d_ff_8_q, d_ff_9_q, d_ff_10_q, not_1_out, or_1_out;

  Clock clock_1 (.out(clock_1_out));
  Clock clock_2 (.out(clock_2_out));
  D_Flip_Flop d_ff_1 (.D(d_ff_3_q), .clk(clock_1_out), .Q(d_ff_1_q), .reset(in_2));  // open: Qn, preset
  LED led_1 (.in(d_ff_1_q));
  D_Flip_Flop d_ff_2 (.D(Input_In), .clk(clock_2_out), .Q(d_ff_2_q), .reset(in_4));  // open: Qn, preset
  LED led_2 (.in(d_ff_2_q));
  not not_1 (not_1_out, in_6);
  and and_1 (and_1_out, in_5, not_1_out);
  and and_2 (and_2_out, in_6, in_7);
  D_Flip_Flop d_ff_3 (.D(d_ff_5_q), .clk(clock_1_out), .Q(d_ff_3_q), .reset(in_2));  // open: Qn, preset
  D_Flip_Flop d_ff_4 (.D(d_ff_2_q), .clk(clock_2_out), .Q(d_ff_4_q), .reset(in_4));  // open: Qn, preset
  LED led_3 (.in(d_ff_3_q));
  LED led_4 (.in(d_ff_4_q));
  or or_1 (or_1_out, and_1_out, and_2_out);
  D_Flip_Flop d_ff_5 (.D(d_ff_7_q), .clk(clock_1_out), .Q(d_ff_5_q), .reset(in_2));  // open: Qn, preset
  D_Flip_Flop d_ff_6 (.D(d_ff_4_q), .clk(clock_2_out), .Q(d_ff_6_q), .reset(in_4));  // open: Qn, preset
  LED led_5 (.in(or_1_out));
  LED led_6 (.in(d_ff_5_q));
  LED led_7 (.in(d_ff_6_q));
  D_Flip_Flop d_ff_7 (.D(d_ff_9_q), .clk(clock_1_out), .Q(d_ff_7_q), .reset(in_2));  // open: Qn, preset
  D_Flip_Flop d_ff_8 (.D(d_ff_6_q), .clk(clock_2_out), .Q(d_ff_8_q), .reset(in_4));  // open: Qn, preset
  LED led_8 (.in(d_ff_7_q));
  LED led_9 (.in(d_ff_8_q));
  D_Flip_Flop d_ff_9 (.D(Data_In), .clk(clock_1_out), .Q(d_ff_9_q), .reset(in_2));  // open: Qn, preset
  D_Flip_Flop d_ff_10 (.D(d_ff_8_q), .clk(clock_2_out), .Q(d_ff_10_q), .reset(in_4));  // open: Qn, preset
  LED led_10 (.in(d_ff_9_q));
  LED led_11 (.in(d_ff_10_q));

  // Notes on the sheet:
  //   Reset Pin
  //   Clock
  //   Reset Pin
  //   Clock
endmodule
