// Logisim project stack_with_registers.circ as structural Verilog: 1 circuit, main circuit main
module main (
  input  in_1,
  input  in_2,
  input  in_3,
  input  in_4
);

  wire and_1_out, and_2_out, and_3_out, and_4_out, and_5_out, and_6_out, and_7_out, and_8_out, and_9_out,
       and_10_out, clock_1_out, d_ff_1_q, d_ff_2_q, d_ff_3_q, d_ff_4_q, d_ff_5_q, d_ff_6_q, d_ff_7_q,
       d_ff_8_q, d_ff_9_q, d_ff_10_q, not_1_out, or_1_out, or_2_out, or_3_out, or_4_out, or_5_out;

  Clock clock_1 (.out(clock_1_out));
  not not_1 (not_1_out, in_1);
  and and_1 (and_1_out, in_1, in_2);
  and and_2 (and_2_out, not_1_out, d_ff_3_q);
  or or_1 (or_1_out, and_1_out, and_2_out);
  D_Flip_Flop d_ff_1 (.D(or_1_out), .clk(clock_1_out), .Q(d_ff_1_q));  // open: Qn, preset, reset
  LED led_1 (.in(d_ff_1_q));
  D_Flip_Flop d_ff_2 (.D(d_ff_1_q), .clk(clock_1_out), .Q(d_ff_2_q), .reset(in_4));  // open: Qn, preset
  and and_3 (and_3_out, in_1, d_ff_1_q);
  and and_4 (and_4_out, not_1_out, d_ff_5_q);
  or or_2 (or_2_out, and_3_out, and_4_out);
  LED led_2 (.in(d_ff_2_q));
  D_Flip_Flop d_ff_3 (.D(or_2_out), .clk(clock_1_out), .Q(d_ff_3_q));  // open: Qn, preset, reset
  LED led_3 (.in(d_ff_3_q));
  D_Flip_Flop d_ff_4 (.D(d_ff_3_q), .clk(clock_1_out), .Q(d_ff_4_q), .reset(in_4));  // open: Qn, preset
  and and_5 (and_5_out, in_1, d_ff_3_q);
  and and_6 (and_6_out, not_1_out, d_ff_7_q);
  or or_3 (or_3_out, and_5_out, and_6_out);
  D_Flip_Flop d_ff_5 (.D(or_3_out), .clk(clock_1_out), .Q(d_ff_5_q));  // open: Qn, preset, reset
  LED led_4 (.in(d_ff_4_q));
  LED led_5 (.in(d_ff_5_q));
  D_Flip_Flop d_ff_6 (.D(d_ff_5_q), .clk(clock_1_out), .Q(d_ff_6_q), .reset(in_4));  // open: Qn, preset
  and and_7 (and_7_out, in_1, d_ff_5_q);
  and and_8 (and_8_out, not_1_out, d_ff_9_q);
  or or_4 (or_4_out, and_7_out, and_8_out);
  D_Flip_Flop d_ff_7 (.D(or_4_out), .clk(clock_1_out), .Q(d_ff_7_q));  // open: Qn, preset, reset
  LED led_6 (.in(d_ff_6_q));
  LED led_7 (.in(d_ff_7_q));
  D_Flip_Flop d_ff_8 (.D(d_ff_7_q), .clk(clock_1_out), .Q(d_ff_8_q), .reset(in_4));  // open: Qn, preset
  and and_9 (and_9_out, in_1, d_ff_7_q);
  and and_10 (and_10_out, not_1_out, in_3);
  or or_5 (or_5_out, and_9_out, and_10_out);
  LED led_8 (.in(d_ff_8_q));
  D_Flip_Flop d_ff_9 (.D(or_5_out), .clk(clock_1_out), .Q(d_ff_9_q));  // open: Qn, preset, reset
  LED led_9 (.in(d_ff_9_q));
  D_Flip_Flop d_ff_10 (.D(d_ff_9_q), .clk(clock_1_out), .Q(d_ff_10_q), .reset(in_4));  // open: Qn, preset
  LED led_10 (.in(d_ff_10_q));
endmodule
